// Logisim project cpu.circ as structural Verilog
module main (
  input  [31:0] in_1
);

  wire AddI, And, Beq, Load, Nor, Or, Resta, Store, Suma;
  wire [7:0] A, B, C, D;

  Multiplexer #(.width(8), .disabled(0), .enable("false")) multiplexer_1 (
    .in1(8'h5f), .out(A), .sel(Suma));  // open: in0
  Multiplexer #(.width(8), .disabled(0), .enable("false")) multiplexer_2 (
    .in1(8'h6e), .out(A), .sel(Resta));  // open: in0
  Multiplexer #(.width(8), .disabled(0), .enable("false")) multiplexer_3 (
    .in1(8'h5f), .out(A), .sel(And));  // open: in0
  Multiplexer #(.width(8), .disabled(0), .enable("false")) multiplexer_4 (.in1(8'h77), .out(A), .sel(Or));  // open: in0
  Multiplexer #(.width(8), .disabled(0), .enable("false")) multiplexer_5 (
    .in1(8'h57), .out(A), .sel(Nor));  // open: in0
  Multiplexer #(.width(8), .disabled(0), .enable("false")) multiplexer_6 (
    .in1(8'h7c), .out(A), .sel(Beq));  // open: in0
  Multiplexer #(.width(8), .disabled(0), .enable("false")) multiplexer_7 (
    .in1(8'h5f), .out(A), .sel(AddI));  // open: in0
  Multiplexer #(.width(8), .disabled(0), .enable("false")) multiplexer_8 (
    .in1(8'h34), .out(A), .sel(Load));  // open: in0
  Multiplexer #(.width(8), .disabled(0), .enable("false")) multiplexer_9 (
    .in1(8'h6e), .out(A), .sel(Store));  // open: in0
  decompose decompose_1 (
    .in_1(in_1), .Suma(Suma), .Resta(Resta), .And(And), .Or(Or), .Nor(Nor), .Beq(Beq), .AddI(AddI),
    .Load(Load), .Store(Store));  // open: Rs, Rt
  Multiplexer #(.width(8), .disabled(0), .enable("false")) multiplexer_10 (
    .in1(8'h79), .out(B), .sel(Suma));  // open: in0
  Multiplexer #(.width(8), .disabled(0), .enable("false")) multiplexer_11 (
    .in1(8'h75), .out(B), .sel(Resta));  // open: in0
  Multiplexer #(.width(8), .disabled(0), .enable("false")) multiplexer_12 (
    .in1(8'h57), .out(B), .sel(And));  // open: in0
  Multiplexer #(.width(8), .disabled(0), .enable("false")) multiplexer_13 (
    .in1(8'h16), .out(B), .sel(Or));  // open: in0
  Multiplexer #(.width(8), .disabled(0), .enable("false")) multiplexer_14 (
    .in1(8'h77), .out(B), .sel(Nor));  // open: in0
  Multiplexer #(.width(8), .disabled(0), .enable("false")) multiplexer_15 (
    .in1(8'h3f), .out(B), .sel(Beq));  // open: in0
  Multiplexer #(.width(8), .disabled(0), .enable("false")) multiplexer_16 (
    .in1(8'h79), .out(B), .sel(AddI));  // open: in0
  Multiplexer #(.width(8), .disabled(0), .enable("false")) multiplexer_17 (
    .in1(8'h77), .out(B), .sel(Load));  // open: in0
  Multiplexer #(.width(8), .disabled(0), .enable("false")) multiplexer_18 (
    .in1(8'h3c), .out(B), .sel(Store));  // open: in0
  Multiplexer #(.width(8), .disabled(0), .enable("false")) multiplexer_19 (
    .in1(8'h79), .out(C), .sel(Suma));  // open: in0
  Multiplexer #(.width(8), .disabled(0), .enable("false")) multiplexer_20 (
    .in1(8'h7c), .out(C), .sel(Resta));  // open: in0
  Multiplexer #(.width(8), .disabled(0), .enable("false")) multiplexer_21 (
    .in1(8'h79), .out(C), .sel(And));  // open: in0
  Multiplexer #(.width(8), .disabled(0), .enable("false")) multiplexer_22 (
    .in1(8'h16), .out(C), .sel(Nor));  // open: in0
  Multiplexer #(.width(8), .disabled(0), .enable("false")) multiplexer_23 (
    .in1(8'h4f), .out(C), .sel(Beq));  // open: in0
  Multiplexer #(.width(8), .disabled(0), .enable("false")) multiplexer_24 (
    .in1(8'h79), .out(C), .sel(AddI));  // open: in0
  Multiplexer #(.width(8), .disabled(0), .enable("false")) multiplexer_25 (
    .in1(8'h5f), .out(C), .sel(Load));  // open: in0
  _7_Segment_Display u_7_segment_display_1 (
    .g(A[3]), .f(A[2]), .a(A[1]), .b(A[0]), .e(A[4]), .d(A[5]), .c(A[6]));  // open: dp
  Multiplexer #(.width(8), .disabled(0), .enable("false")) multiplexer_26 (
    .in1(8'h14), .out(D), .sel(AddI));  // open: in0
  Multiplexer #(.width(8), .disabled(0), .enable("false")) multiplexer_27 (
    .in1(8'h79), .out(D), .sel(Load));  // open: in0
  _7_Segment_Display u_7_segment_display_2 (
    .g(B[3]), .f(B[2]), .a(B[1]), .b(B[0]), .e(B[4]), .d(B[5]), .c(B[6]));  // open: dp
  _7_Segment_Display u_7_segment_display_3 (
    .g(C[3]), .f(C[2]), .a(C[1]), .b(C[0]), .e(C[4]), .d(C[5]), .c(C[6]));  // open: dp
  _7_Segment_Display u_7_segment_display_4 (
    .g(D[3]), .f(D[2]), .a(D[1]), .b(D[0]), .e(D[4]), .d(D[5]), .c(D[6]));  // open: dp
endmodule

module decompose (
  input  [31:0] in_1,
  output [4:0] Rs,
  output [4:0] Rt,
  output Suma,
  output Resta,
  output And,
  output Or,
  output Nor,
  output Beq,
  output AddI,
  output Load,
  output Store
);

  wire comparator_1_eq, comparator_2_eq, comparator_3_eq, comparator_4_eq, comparator_6_eq, comparator_7_eq,
       comparator_8_eq, comparator_9_eq, comparator_10_eq, not_1_out, not_2_out, not_3_out, not_4_out, Tipo_R;

  Comparator #(.width(6)) comparator_1 (.a(in_1[5:0]), .b(6'b100000), .eq(comparator_1_eq));  // open: gt, lt
  not not_1 (not_1_out, Tipo_R);
  Comparator #(.width(6)) comparator_2 (.a(in_1[31:26]), .b(6'b000100), .eq(comparator_2_eq));  // open: gt, lt
  and and_1 (Suma, Tipo_R, comparator_1_eq);
  and and_2 (Beq, not_1_out, comparator_2_eq);
  Comparator #(.width(6)) comparator_3 (.a(in_1[5:0]), .b(6'b100010), .eq(comparator_3_eq));  // open: gt, lt
  Comparator #(.width(6)) comparator_4 (.a(in_1[31:26]), .b(6'b001000), .eq(comparator_4_eq));  // open: gt, lt
  and and_3 (Resta, Tipo_R, comparator_3_eq);
  not not_2 (not_2_out, Tipo_R);
  and and_4 (AddI, not_2_out, comparator_4_eq);
  Comparator #(.width(6)) comparator_5 (.a(in_1[31:26]), .b({6{1'b0}}), .eq(Tipo_R));  // open: gt, lt
  Comparator #(.width(6)) comparator_6 (.a(in_1[5:0]), .b(6'b100100), .eq(comparator_6_eq));  // open: gt, lt
  and and_5 (And, Tipo_R, comparator_6_eq);
  not not_3 (not_3_out, Tipo_R);
  Comparator #(.width(6)) comparator_7 (.a(in_1[31:26]), .b(6'b100011), .eq(comparator_7_eq));  // open: gt, lt
  and and_6 (Load, not_3_out, comparator_7_eq);
  Comparator #(.width(6)) comparator_8 (.a(in_1[5:0]), .b(6'b100101), .eq(comparator_8_eq));  // open: gt, lt
  Comparator #(.width(6)) comparator_9 (.a(in_1[31:26]), .b(6'b101011), .eq(comparator_9_eq));  // open: gt, lt
  and and_7 (Or, Tipo_R, comparator_8_eq);
  not not_4 (not_4_out, Tipo_R);
  and and_8 (Store, not_4_out, comparator_9_eq);
  Comparator #(.width(6)) comparator_10 (.a(in_1[5:0]), .b(6'b100111), .eq(comparator_10_eq));  // open: gt, lt
  and and_9 (Nor, Tipo_R, comparator_10_eq);

  assign Rs = in_1[20:16];
  assign Rt = in_1[25:21];

  // Other names for the same wires on the sheet: Address[15:0] = in_1[15:0]; Funct[5:0] = in_1[5:0];
  //   Rd[4:0] = in_1[15:11]; OpCode[5:0] = in_1[31:26]
endmodule

module pc (
  input  clk,
  output [31:0] data
);

  wire [7:0] register_1_q_2;
  wire [23:0] register_1_q;
  wire [31:0] adder_1_out;

  Register #(.width(32)) register_1 (.D(adder_1_out), .Q({register_1_q_2, register_1_q}), .clk(clk));  // open: en, clr
  Adder #(.width(32)) adder_1 (.a(32'h1), .b({register_1_q_2, register_1_q}), .out(adder_1_out));  // open: cin, cout
  ROM rom_1 (.pos(register_1_q), .data(data));  // open: sel
endmodule

module RAM (
  input  [23:0] pos,
  input  [31:0] data,
  input  sel,
  input  clk,
  input  ld,
  input  clr
);

  RAM_part #(.addrWidth(24), .dataWidth(32)) ram_1 (.addr(pos), .data(data), .sel(sel), .clk(clk), .ld(ld), .clr(clr));
endmodule

module ROM (
  input  [23:0] pos,
  input  sel,
  output [31:0] data
);

  ROM_part #(.addrWidth(24), .dataWidth(32)) rom_1 (.addr(pos), .data(data), .sel(sel));
endmodule
